// Logisim project DaBoizmips.circ as structural Verilog: 9 circuits, main circuit TG00MIPS
module TG00MIPS (
);

  wire CLK_out, stopclk_1_p1, stopclk_1_p3;

  Clock #(.highDuration(8), .lowDuration(8)) CLK (.out(CLK_out));
  // StopClk stopclk_1: pin names not known; wires that end beside it: stopclk_1_p1, CLK_out, stopclk_1_p3
  MIPS mips_1 (.clk(stopclk_1_p3), .reset(1'b0), .halt(stopclk_1_p1));
endmodule

// clk
module MIPS (
  input  clk,
  input  reset,
  output halt
);

  wire abs, alu_1_z, and_1_out, cu_1_alusrc, cu_1_beq, cu_1_jump, cu_1_lw, cu_1_rw, cu_1_selm, cu_1_wm,
       not_1_out, sela, SELP;
  wire [1:0] OP;
  wire [3:0] control_alu_1_out;
  wire [4:0] instdecoder_1_ib15_11__rd, instdecoder_1_ib20_16__rt, instdecoder_1_ib25_21__rs,
       multiplexer_6_out;
  wire [5:0] func, instdecoder_1_ib31_26__opc;
  wire [15:0] instdecoder_1_ib15_0__imm;
  wire [25:0] instdecoder_1_ib25_0__addr;
  wire [31:0] adder_1_out, adder_2_out, alu_1_result, bit_extender_1_out, bit_extender_2_out,
       data_memory_32_1_read_data, instruction_memory_1_instruction, min, multiplexer_1_out,
       multiplexer_2_out, multiplexer_3_out, multiplexer_4_out, multiplexer_5_out, multiplexer_7_out, PC_q,
       register_file_1_read_data_1, register_file_1_read_data_2, shifter_1_out, shifter_2_out;

  assign bit_extender_1_out = {{6{instdecoder_1_ib25_0__addr[25]}}, instdecoder_1_ib25_0__addr};  // Bit_Extender bit_extender_1
  Adder #(.width(32)) adder_1 (.a(adder_2_out), .b(shifter_1_out), .out(adder_1_out));  // open: cin, cout
  Shifter #(.width(32)) shifter_1 (.in(bit_extender_2_out), .\dist (5'b00010), .out(shifter_1_out));
  and and_1 (and_1_out, alu_1_z, cu_1_beq);
  Multiplexer #(.width(32), .enable("false")) multiplexer_1 (
    .in0(adder_2_out), .in1(shifter_2_out), .out(multiplexer_1_out), .sel(cu_1_jump));
  Shifter #(.width(32)) shifter_2 (.in(bit_extender_1_out), .\dist (5'b00010), .out(shifter_2_out));
  Multiplexer #(.width(32), .enable("false")) multiplexer_2 (
    .in0(data_memory_32_1_read_data), .in1(alu_1_result), .out(multiplexer_2_out), .sel(cu_1_selm));
  Multiplexer #(.width(32), .enable("false")) multiplexer_3 (
    .in0(multiplexer_1_out), .in1(adder_1_out), .out(multiplexer_3_out), .sel(and_1_out));
  Register #(.width(32)) PC (.D(multiplexer_3_out), .en(not_1_out), .Q(PC_q), .clk(clk), .clr(reset));
  not not_1 (not_1_out, halt);
  Adder #(.width(32)) adder_2 (.a(32'h4), .b(PC_q), .out(adder_2_out));  // open: cin, cout
  Multiplexer #(.width(32), .enable("false")) multiplexer_4 (
    .in0(register_file_1_read_data_1), .in1(min), .out(multiplexer_4_out), .sel(sela));
  Multiplexer #(.width(32), .enable("false")) multiplexer_5 (
    .in0(multiplexer_2_out), .in1(multiplexer_4_out), .out(multiplexer_5_out), .sel(abs));
  Multiplexer #(.width(5), .enable("false")) multiplexer_6 (
    .in0(instdecoder_1_ib20_16__rt), .in1(instdecoder_1_ib15_11__rd), .out(multiplexer_6_out), .sel(SELP));
  Register_file register_file_1 (
    .Read_Register_1(instdecoder_1_ib25_21__rs), .Read_Register_2(instdecoder_1_ib20_16__rt),
    .Write_Register(multiplexer_6_out), .Write_Data(multiplexer_5_out),
    .Read_Data_1(register_file_1_read_data_1), .Read_Data_2(register_file_1_read_data_2), .clk(clk),
    .reset(reset), .Write(cu_1_rw));
  Instruction_memory instruction_memory_1 (.Read_address(PC_q), .Instruction(instruction_memory_1_instruction));
  Control_ALU control_alu_1 (.OpALU(OP), .funcion(func), .OUT(control_alu_1_out));
  Multiplexer #(.width(32), .enable("false")) multiplexer_7 (
    .in0(bit_extender_2_out), .in1(register_file_1_read_data_2), .out(multiplexer_7_out), .sel(cu_1_alusrc));
  ALU alu_1 (
    .A(register_file_1_read_data_1), .B(multiplexer_7_out), .Z(alu_1_z), .Result(alu_1_result),
    .Operation(control_alu_1_out));
  assign bit_extender_2_out = {{16{instdecoder_1_ib15_0__imm[15]}}, instdecoder_1_ib15_0__imm};  // Bit_Extender bit_extender_2
  InstDecoder instdecoder_1 (
    .IB(instruction_memory_1_instruction), .IB31_26__opc(instdecoder_1_ib31_26__opc),
    .IB25_21__rs(instdecoder_1_ib25_21__rs), .IB20_16__rt(instdecoder_1_ib20_16__rt),
    .IB15_11__rd(instdecoder_1_ib15_11__rd), .IB5_0__func(func), .IB15_0__imm(instdecoder_1_ib15_0__imm),
    .IB25_0__addr(instdecoder_1_ib25_0__addr));
  Comparator #(.width(32)) comparator_1 (.a({32{1'b0}}), .b(register_file_1_read_data_1), .gt(sela));  // open: eq, lt
  CU cu_1 (
    .opc0(instdecoder_1_ib31_26__opc[5]), .opc1(instdecoder_1_ib31_26__opc[4]),
    .opc2(instdecoder_1_ib31_26__opc[3]), .opc3(instdecoder_1_ib31_26__opc[2]),
    .opc4(instdecoder_1_ib31_26__opc[1]), .opc5(instdecoder_1_ib31_26__opc[0]), .halt(halt),
    .jump(cu_1_jump), .RW(cu_1_rw), .LW(cu_1_lw), .SELM(cu_1_selm), .WM(cu_1_wm), .ALUSrc(cu_1_alusrc),
    .op0(OP[1]), .op1(OP[0]), .SELP(SELP), .beq(cu_1_beq), .abs(abs));
  Subtractor #(.width(32)) subtractor_1 (
    .a({32{1'b0}}), .b(register_file_1_read_data_1), .out(min));  // open: bin, bout
  Data_Memory_32 data_memory_32_1 (
    .Address(alu_1_result), .Write_Data(register_file_1_read_data_2), .Read_Data(data_memory_32_1_read_data),
    .Write(cu_1_wm), .clk(clk), .reset(reset), .Read(cu_1_lw));
endmodule

module Register_file (
  input  clk,
  input  reset,
  input  [4:0] Read_Register_1,
  input  [4:0] Read_Register_2,
  input  [4:0] Write_Register,
  input  [31:0] Write_Data,
  input  Write,
  output [31:0] Read_Data_1,
  output [31:0] Read_Data_2
);

  wire decoder_1_out1, decoder_1_out2, decoder_1_out3, decoder_1_out4, decoder_1_out5, decoder_1_out6,
       decoder_1_out7, decoder_1_out8, decoder_1_out9, decoder_1_out10, decoder_1_out11, decoder_1_out12,
       decoder_1_out13, decoder_1_out14, decoder_1_out15, decoder_1_out16, decoder_1_out17, decoder_1_out18,
       decoder_1_out19, decoder_1_out20, decoder_1_out21, decoder_1_out22, decoder_1_out23, decoder_1_out24,
       decoder_1_out25, decoder_1_out26, decoder_1_out27, decoder_1_out28, decoder_1_out29, decoder_1_out30,
       decoder_1_out31;
  wire [31:0] delayer1x32_1_p2, multiplexer_1_out, multiplexer_2_out, R1_q, R2_q, R3_q, R4_q, R5_q, R6_q,
       R7_q, R8_q, R9_q, R10_q, R11_q, R12_q, R13_q, R14_q, R15_q, R16_q, R17_q, R18_q, R19_q, R20_q, R21_q,
       R22_q, R23_q, R24_q, R25_q, R26_q, R27_q, R28_q, R29_q, R30_q, R31_q;

  Decoder #(.select(5), .disabled(0)) decoder_1 (
    .out1(decoder_1_out1), .out2(decoder_1_out2), .out3(decoder_1_out3), .out4(decoder_1_out4),
    .out5(decoder_1_out5), .out6(decoder_1_out6), .out7(decoder_1_out7), .out8(decoder_1_out8),
    .out9(decoder_1_out9), .out10(decoder_1_out10), .out11(decoder_1_out11), .out12(decoder_1_out12),
    .out13(decoder_1_out13), .out14(decoder_1_out14), .out15(decoder_1_out15), .out16(decoder_1_out16),
    .out17(decoder_1_out17), .out18(decoder_1_out18), .out19(decoder_1_out19), .out20(decoder_1_out20),
    .out21(decoder_1_out21), .out22(decoder_1_out22), .out23(decoder_1_out23), .out24(decoder_1_out24),
    .out25(decoder_1_out25), .out26(decoder_1_out26), .out27(decoder_1_out27), .out28(decoder_1_out28),
    .out29(decoder_1_out29), .out30(decoder_1_out30), .out31(decoder_1_out31), .sel(Write_Register),
    .en(Write));  // open: out0
  // Delayer1x32 delayer1x32_1: pin names not known; wires that end beside it: Write_Data, delayer1x32_1_p2
  Register #(.width(32)) R1 (.D(delayer1x32_1_p2), .en(decoder_1_out1), .Q(R1_q), .clk(clk), .clr(reset));
  Register #(.width(32)) R2 (.D(delayer1x32_1_p2), .en(decoder_1_out2), .Q(R2_q), .clk(clk), .clr(reset));
  Register #(.width(32)) R3 (.D(delayer1x32_1_p2), .en(decoder_1_out3), .Q(R3_q), .clk(clk), .clr(reset));
  Register #(.width(32)) R4 (.D(delayer1x32_1_p2), .en(decoder_1_out4), .Q(R4_q), .clk(clk), .clr(reset));
  Register #(.width(32)) R5 (.D(delayer1x32_1_p2), .en(decoder_1_out5), .Q(R5_q), .clk(clk), .clr(reset));
  Register #(.width(32)) R6 (.D(delayer1x32_1_p2), .en(decoder_1_out6), .Q(R6_q), .clk(clk), .clr(reset));
  Register #(.width(32)) R7 (.D(delayer1x32_1_p2), .en(decoder_1_out7), .Q(R7_q), .clk(clk), .clr(reset));
  Register #(.width(32)) R8 (.D(delayer1x32_1_p2), .en(decoder_1_out8), .Q(R8_q), .clk(clk), .clr(reset));
  Register #(.width(32)) R9 (.D(delayer1x32_1_p2), .en(decoder_1_out9), .Q(R9_q), .clk(clk), .clr(reset));
  Register #(.width(32)) R10 (.D(delayer1x32_1_p2), .en(decoder_1_out10), .Q(R10_q), .clk(clk), .clr(reset));
  Register #(.width(32)) R11 (.D(delayer1x32_1_p2), .en(decoder_1_out11), .Q(R11_q), .clk(clk), .clr(reset));
  Register #(.width(32)) R12 (.D(delayer1x32_1_p2), .en(decoder_1_out12), .Q(R12_q), .clk(clk), .clr(reset));
  Register #(.width(32)) R13 (.D(delayer1x32_1_p2), .en(decoder_1_out13), .Q(R13_q), .clk(clk), .clr(reset));
  Register #(.width(32)) R14 (.D(delayer1x32_1_p2), .en(decoder_1_out14), .Q(R14_q), .clk(clk), .clr(reset));
  Register #(.width(32)) R15 (.D(delayer1x32_1_p2), .en(decoder_1_out15), .Q(R15_q), .clk(clk), .clr(reset));
  Register #(.width(32)) R16 (.D(delayer1x32_1_p2), .en(decoder_1_out16), .Q(R16_q), .clk(clk), .clr(reset));
  Register #(.width(32)) R17 (.D(delayer1x32_1_p2), .en(decoder_1_out17), .Q(R17_q), .clk(clk), .clr(reset));
  Register #(.width(32)) R18 (.D(delayer1x32_1_p2), .en(decoder_1_out18), .Q(R18_q), .clk(clk), .clr(reset));
  Register #(.width(32)) R19 (.D(delayer1x32_1_p2), .en(decoder_1_out19), .Q(R19_q), .clk(clk), .clr(reset));
  Register #(.width(32)) R20 (.D(delayer1x32_1_p2), .en(decoder_1_out20), .Q(R20_q), .clk(clk), .clr(reset));
  Register #(.width(32)) R21 (.D(delayer1x32_1_p2), .en(decoder_1_out21), .Q(R21_q), .clk(clk), .clr(reset));
  Register #(.width(32)) R22 (.D(delayer1x32_1_p2), .en(decoder_1_out22), .Q(R22_q), .clk(clk), .clr(reset));
  Register #(.width(32)) R23 (.D(delayer1x32_1_p2), .en(decoder_1_out23), .Q(R23_q), .clk(clk), .clr(reset));
  Register #(.width(32)) R24 (.D(delayer1x32_1_p2), .en(decoder_1_out24), .Q(R24_q), .clk(clk), .clr(reset));
  Register #(.width(32)) R25 (.D(delayer1x32_1_p2), .en(decoder_1_out25), .Q(R25_q), .clk(clk), .clr(reset));
  Register #(.width(32)) R26 (.D(delayer1x32_1_p2), .en(decoder_1_out26), .Q(R26_q), .clk(clk), .clr(reset));
  Register #(.width(32)) R27 (.D(delayer1x32_1_p2), .en(decoder_1_out27), .Q(R27_q), .clk(clk), .clr(reset));
  Register #(.width(32)) R28 (.D(delayer1x32_1_p2), .en(decoder_1_out28), .Q(R28_q), .clk(clk), .clr(reset));
  Register #(.width(32)) R29 (.D(delayer1x32_1_p2), .en(decoder_1_out29), .Q(R29_q), .clk(clk), .clr(reset));
  Register #(.width(32)) R30 (.D(delayer1x32_1_p2), .en(decoder_1_out30), .Q(R30_q), .clk(clk), .clr(reset));
  Register #(.width(32)) R31 (.D(delayer1x32_1_p2), .en(decoder_1_out31), .Q(R31_q), .clk(clk), .clr(reset));
  Multiplexer #(.select(5), .width(32), .enable("false")) multiplexer_1 (
    .in0({32{1'b0}}), .in1(R1_q), .in2(R2_q), .in3(R3_q), .in4(R4_q), .in5(R5_q), .in6(R6_q), .in7(R7_q),
    .in8(R8_q), .in9(R9_q), .in10(R10_q), .in11(R11_q), .in12(R12_q), .in13(R13_q), .in14(R14_q),
    .in15(R15_q), .in16(R16_q), .in17(R17_q), .in18(R18_q), .in19(R19_q), .in20(R20_q), .in21(R21_q),
    .in22(R22_q), .in23(R23_q), .in24(R24_q), .in25(R25_q), .in26(R26_q), .in27(R27_q), .in28(R28_q),
    .in29(R29_q), .in30(R30_q), .in31(R31_q), .out(multiplexer_1_out), .sel(Read_Register_1));
  Multiplexer #(.select(5), .width(32), .enable("false")) multiplexer_2 (
    .in0({32{1'b0}}), .in1(R1_q), .in2(R2_q), .in3(R3_q), .in4(R4_q), .in5(R5_q), .in6(R6_q), .in7(R7_q),
    .in8(R8_q), .in9(R9_q), .in10(R10_q), .in11(R11_q), .in12(R12_q), .in13(R13_q), .in14(R14_q),
    .in15(R15_q), .in16(R16_q), .in17(R17_q), .in18(R18_q), .in19(R19_q), .in20(R20_q), .in21(R21_q),
    .in22(R22_q), .in23(R23_q), .in24(R24_q), .in25(R25_q), .in26(R26_q), .in27(R27_q), .in28(R28_q),
    .in29(R29_q), .in30(R30_q), .in31(R31_q), .out(multiplexer_2_out), .sel(Read_Register_2));
  // Delayer1x32 delayer1x32_2: pin names not known; wires that end beside it: multiplexer_1_out, Read_Data_1
  // Delayer1x32 delayer1x32_3: pin names not known; wires that end beside it: multiplexer_2_out, Read_Data_2
endmodule

module ALU (
  input  [3:0] Operation,
  input  [31:0] A,
  input  [31:0] B,
  output Z,
  output [31:0] Result
);

  wire nor_1_out;
  wire [0:0] comparator_1_lt;
  wire [31:0] adder_1_out, and_1_out, multiplexer_1_out, multiplexer_2_out, multiplexer_3_out, not_1_out,
       not_2_out, or_1_out;

  assign not_1_out = ~A;  // NOT_Gate not_1, 32 bits wide
  assign not_2_out = ~B;  // NOT_Gate not_2, 32 bits wide
  Comparator #(.width(32)) comparator_1 (.a(A), .b(B), .lt(comparator_1_lt[0]));  // open: gt, eq
  Multiplexer #(.width(32), .enable("false")) multiplexer_1 (
    .in0(A), .in1(not_1_out), .out(multiplexer_1_out), .sel(Operation[3]));
  Multiplexer #(.width(32), .enable("false")) multiplexer_2 (
    .in0(B), .in1(not_2_out), .out(multiplexer_2_out), .sel(Operation[2]));
  assign and_1_out = multiplexer_1_out & multiplexer_2_out;  // AND_Gate and_1, 32 bits wide
  assign or_1_out = multiplexer_1_out | multiplexer_2_out;  // OR_Gate or_1, 32 bits wide
  Adder #(.width(32)) adder_1 (
    .a(multiplexer_1_out), .b(multiplexer_2_out), .out(adder_1_out), .cin(Operation[2]));  // open: cout
  Multiplexer #(.select(2), .width(32), .enable("false")) multiplexer_3 (
    .in0(and_1_out), .in1(or_1_out), .in2(adder_1_out), .in3({{31{1'b0}}, comparator_1_lt[0]}),
    .out(multiplexer_3_out), .sel(Operation[1:0]));
  nor nor_1 (nor_1_out, multiplexer_3_out[0], multiplexer_3_out[1], multiplexer_3_out[2], multiplexer_3_out[3], multiplexer_3_out[4], multiplexer_3_out[5], multiplexer_3_out[6], multiplexer_3_out[7], multiplexer_3_out[8], multiplexer_3_out[9], multiplexer_3_out[10], multiplexer_3_out[11], multiplexer_3_out[12], multiplexer_3_out[13], multiplexer_3_out[14], multiplexer_3_out[15], multiplexer_3_out[16], multiplexer_3_out[17], multiplexer_3_out[18], multiplexer_3_out[19], multiplexer_3_out[20], multiplexer_3_out[21], multiplexer_3_out[22], multiplexer_3_out[23], multiplexer_3_out[24], multiplexer_3_out[25], multiplexer_3_out[26], multiplexer_3_out[27], multiplexer_3_out[28], multiplexer_3_out[29], multiplexer_3_out[30], multiplexer_3_out[31]);
  // Delayer2x32 delayer2x32_1: pin names not known; wires that end beside it: multiplexer_3_out, Result
  // Delayer2x1 delayer2x1_1: pin names not known; wires that end beside it: nor_1_out, Z

  // Notes on the sheet:
  //   0001    OR
  //   Operation    Function
  //   0000    AND
  //   0010    add
  //   0110    subtract
  //   0111    set on less than
  //   1100    NOR
endmodule

module Data_Memory_32 (
  input  Write,
  input  [31:0] Address,
  input  [31:0] Write_Data,
  input  clk,
  input  reset,
  input  Read,
  output [31:0] Read_Data
);

  wire [9:0] bitselector_1_out;
  wire [31:0] delayer2x32_1_p2, ram_1_data;

  BitSelector #(.width(32), .group(10)) bitselector_1 (.in(Address), .out(bitselector_1_out), .sel(2'b00));
  // Delayer2x32 delayer2x32_1: pin names not known; wires that end beside it: Write_Data, delayer2x32_1_p2
  RAM #(.dataWidth(32), .bus("separate"), .Datafile_on_reset("TG00ram.txt")) ram_1 (
    .addr(bitselector_1_out[9:2]), .din(delayer2x32_1_p2), .data(ram_1_data), .str(Write), .sel(1'b1),
    .clk(clk), .ld(Read), .clr(reset));
  // Delayer2x32 delayer2x32_2: pin names not known; wires that end beside it: ram_1_data, Read_Data

  // Notes on the sheet:
  //   Memoria de 32 bits direccionable a nivel de byte
  //   Tan solo implementadas las 256 primeras posiciones de 32 bits o 1024 bytes
endmodule

module Instruction_memory (
  input  [31:0] Read_address,
  output [31:0] Instruction
);

  wire [6:0] bitselector_1_out;
  wire [31:0] ram_1_data;

  BitSelector #(.width(30), .group(7)) bitselector_1 (.in(Read_address[31:2]), .out(bitselector_1_out), .sel(3'b000));
  RAM #(.addrWidth(7), .dataWidth(32), .bus("asynch"), .Datafile_on_reset("TG00MIPS.txt")) ram_1 (
    .addr(bitselector_1_out), .data(ram_1_data), .sel(1'b1), .ld(1'b1), .clr(1'b0));
  // Delayer2x32 delayer2x32_1: pin names not known; wires that end beside it: ram_1_data, Instruction
endmodule

module InstDecoder (
  input  [31:0] IB,
  output [5:0] IB31_26__opc,
  output [4:0] IB25_21__rs,
  output [4:0] IB20_16__rt,
  output [4:0] IB15_11__rd,
  output [5:0] IB5_0__func,
  output [15:0] IB15_0__imm,
  output [25:0] IB25_0__addr
);


  assign IB5_0__func = IB[5:0];
  assign IB15_0__imm = IB[15:0];
  assign IB15_11__rd = IB[15:11];
  assign IB20_16__rt = IB[20:16];
  assign IB25_0__addr = IB[25:0];
  assign IB25_21__rs = IB[25:21];
  assign IB31_26__opc = IB[31:26];
endmodule

module Control_ALU (
  input  [1:0] OpALU,
  input  [5:0] funcion,
  output [3:0] OUT
);

  wire [3:0] multiplexer_1_out;

  Multiplexer #(.select(4), .width(4), .enable("false")) multiplexer_1 (
    .in0(4'b0010), .in2(4'b0110), .in4(4'b0000), .in5(4'b0001), .in10(4'b0111), .out(multiplexer_1_out),
    .sel(funcion[3:0]));  // open: in1, in3, in6, in7, in8, in9, in11, in12, in13, in14, in15
  Multiplexer #(.select(2), .width(4), .enable("false")) multiplexer_2 (
    .in0(4'b0010), .in1(4'b0110), .in2(multiplexer_1_out), .out(OUT), .sel(OpALU));  // open: in3
endmodule

module CU (
  input  opc0,
  input  opc1,
  input  opc2,
  input  opc3,
  input  opc4,
  input  opc5,
  output halt,
  output jump,
  output RW,
  output LW,
  output SELM,
  output WM,
  output ALUSrc,
  output op0,
  output op1,
  output SELP,
  output beq,
  output abs
);

  wire and_2_out, and_3_out, and_4_out, and_5_out, and_6_out, and_7_out, and_8_out, and_9_out, and_10_out,
       and_11_out, and_12_out, and_13_out, and_14_out, and_15_out, and_16_out, and_18_out, and_19_out,
       and_20_out, and_21_out, not_1_out, not_2_out, not_3_out, not_4_out, not_5_out, not_6_out, not_7_out,
       not_8_out, not_9_out, not_10_out, not_11_out, not_12_out, not_13_out, not_14_out, not_15_out,
       not_16_out, not_17_out, not_18_out, not_20_out, not_21_out, not_22_out, not_23_out, not_24_out,
       not_25_out, not_26_out, not_27_out, not_28_out, not_29_out, not_30_out, not_31_out, not_32_out,
       not_33_out, not_34_out, not_35_out, not_36_out, not_37_out, not_38_out, not_39_out, not_40_out,
       not_41_out, not_42_out, not_43_out, not_44_out, not_45_out, not_46_out, not_47_out, not_48_out,
       not_49_out, not_50_out;

  not not_1 (not_1_out, opc0);
  not not_2 (not_2_out, opc2);
  not not_3 (not_3_out, opc2);
  not not_4 (not_4_out, opc4);
  not not_5 (not_5_out, opc2);
  not not_6 (not_6_out, opc2);
  not not_7 (not_7_out, opc4);
  not not_8 (not_8_out, opc2);
  not not_9 (not_9_out, opc5);
  not not_10 (not_10_out, opc3);
  not not_11 (not_11_out, opc4);
  not not_12 (not_12_out, opc4);
  not not_13 (not_13_out, opc4);
  not not_14 (not_14_out, opc4);
  not not_15 (not_15_out, opc4);
  not not_16 (not_16_out, opc1);
  not not_17 (not_17_out, opc2);
  not not_18 (not_18_out, opc3);
  not not_19 (SELM, opc4);
  and and_1 (WM, opc0, opc2);
  not not_20 (not_20_out, opc2);
  not not_21 (not_21_out, opc4);
  not not_22 (not_22_out, opc5);
  not not_23 (not_23_out, opc2);
  not not_24 (not_24_out, opc4);
  not not_25 (not_25_out, opc2);
  not not_26 (not_26_out, opc4);
  not not_27 (not_27_out, opc2);
  not not_28 (not_28_out, opc4);
  not not_29 (not_29_out, opc2);
  not not_30 (not_30_out, opc3);
  not not_31 (not_31_out, opc4);
  not not_32 (not_32_out, opc2);
  not not_33 (not_33_out, opc4);
  not not_34 (not_34_out, opc5);
  not not_35 (not_35_out, opc2);
  not not_36 (not_36_out, opc4);
  not not_37 (not_37_out, opc2);
  not not_38 (not_38_out, opc4);
  not not_39 (not_39_out, opc2);
  not not_40 (not_40_out, opc4);
  not not_41 (not_41_out, opc0);
  not not_42 (not_42_out, opc1);
  not not_43 (not_43_out, opc2);
  not not_44 (not_44_out, opc4);
  not not_45 (not_45_out, opc5);
  not not_46 (not_46_out, opc0);
  not not_47 (not_47_out, opc1);
  not not_48 (not_48_out, opc2);
  not not_49 (not_49_out, opc3);
  not not_50 (not_50_out, opc4);
  and and_2 (and_2_out, not_1_out, not_2_out, opc4);
  and and_3 (and_3_out, not_3_out, opc3, not_4_out, opc5);
  and and_4 (and_4_out, opc1, not_5_out);
  and and_5 (and_5_out, opc0, not_6_out, not_7_out);
  and and_6 (and_6_out, opc0, not_8_out, not_9_out);
  and and_7 (and_7_out, not_10_out, not_11_out);
  and and_8 (and_8_out, not_12_out, opc5);
  and and_9 (and_9_out, opc2, not_13_out);
  and and_10 (and_10_out, opc1, not_14_out);
  and and_11 (and_11_out, opc0, not_15_out);
  and and_12 (and_12_out, opc0, not_16_out, not_17_out, not_18_out, opc5);
  and and_13 (and_13_out, not_20_out, not_21_out, not_22_out);
  and and_14 (and_14_out, not_23_out, opc3, not_24_out);
  and and_15 (and_15_out, opc1, not_25_out, not_26_out);
  and and_16 (and_16_out, opc0, not_27_out, not_28_out);
  and and_17 (op0, not_29_out, not_30_out, not_31_out);
  and and_18 (and_18_out, not_32_out, not_33_out, not_34_out);
  and and_19 (and_19_out, not_35_out, opc3, not_36_out);
  and and_20 (and_20_out, opc1, not_37_out, not_38_out);
  and and_21 (and_21_out, opc0, not_39_out, not_40_out);
  and and_22 (beq, not_41_out, not_42_out, not_43_out, opc3, not_44_out, not_45_out);
  and and_23 (abs, not_46_out, not_47_out, not_48_out, not_49_out, not_50_out, opc5);
  or or_1 (jump, and_2_out, and_3_out, and_4_out, and_5_out, and_6_out);
  or or_2 (RW, and_7_out, and_8_out, and_9_out, and_10_out, and_11_out, and_12_out);
  or or_3 (ALUSrc, and_13_out, and_14_out, and_15_out, and_16_out);
  or or_4 (SELP, and_18_out, and_19_out, and_20_out, and_21_out);

  assign halt = opc1;
  assign LW = opc0;
  assign op1 = opc3;
endmodule
